# Fritzing sketch SerialLED_MiniPro (saved by Fritzing 0.9.3b)
breadboards: 1

parts:
  元件1 = Arduino Nano (Rev3.0) (ICSP)
  R1 = Resistor [tolerance=±5% resistance=220 package=THT]
  LED1 = LED - 5mm [color="Red (633nm)" package="5 mm [THT]"]
  RGB_SMD_LED1 = SMD RGB LED (WS2812) [package=5050]  # not connected

nets:
  N1: 元件1.GND, LED1.cathode
  N2: 元件1.A1, R1.Pin_1, LED1.anode
  N3: 元件1.D13/SCK, R1.Pin_0
